// Logisim project cgu.circ as structural Verilog: 1 circuit, main circuit main
module main (
  input  ps0,
  input  ps1,
  input  gs0,
  input  gs1,
  input  ci,
  output out_6,
  output c0
);

  wire and_1_out, and_3_out, and_4_out, or_1_out, or_2_out, or_3_out;

  or or_1 (or_1_out, ps0, gs0);
  or or_2 (or_2_out, ps1, gs1);
  and and_1 (and_1_out, gs0, or_2_out);
  and and_2 (c0, or_1_out, ci);
  or or_3 (or_3_out, ps1, and_1_out);
  and and_3 (and_3_out, ps0, or_3_out);
  and and_4 (and_4_out, and_3_out, ci);
endmodule
